# Fritzing sketch Final-HORN (saved by Fritzing 0.7.7b)

parts:
  VCC1 = Battery  # not connected
  Arduino1 = Arduino
  S1 = Round Pushbutton
  J1 = Piezo Speaker

nets:
  N1: Arduino1.D12, J1.pin2
  N2: Arduino1.D3, S1.leg1
  N3: Arduino1.GND, S1.leg0
