# Fritzing sketch Final-LEDS (saved by Fritzing 0.7.7b)

parts:
  VCC1 = Battery  # not connected
  Arduino1 = Arduino
  S1 = Round Pushbutton
  S2 = Square Pushbutton
  Part1 = LED Matrix - Serial Interface - Red/Green/Blue

nets:
  N1: Arduino1.GND, S2.leg0
  N2: Arduino1.D3, S1.leg1
  N3: Arduino1.D2, S2.leg1
  N4: Arduino1.A0, Part1.SCK
  N5: Arduino1.A1, Arduino1.A2, Part1.VCC
  N6: Arduino1.A4, Part1.CS
  N7: Arduino1.A5, Part1.MOSI
